// Logisim project ARM_CPU.circ as structural Verilog
module main (
);

  FD fd_1 ();
  Fetch fetch_1 ();  // open: Inst
  Decode decode_1 ();
  DE de_1 ();
  Execute execute_1 ();
  EM em_1 ();
  MW mw_1 ();
  Memory memory_1 ();
endmodule

module Fetch (
  input  [31:0] Inst
);


  // Other names for the same wires on the sheet: Cond[3:0] = Inst[31:28]; DestReg[3:0] = Inst[15:12];
  //   Format[1:0] = Inst[27:26]; InputReg[3:0] = Inst[19:16]; SCF = Inst[20]; Imm = Inst[25];
  //   OpCode[3:0] = Inst[24:21]; Operand2[11:0] = Inst[11:0]

  // Notes on the sheet:
  //   operand 2
  //   rd
  //   rn
  //   set cond flags
  //   op code
  //   immediate
  //   format
  //   conditional
endmodule
